// Logisim project GateCircuit.circ as structural Verilog: 1 circuit, main circuit main
module main (
  input  A,
  input  B,
  input  in_3,
  input  in_4,
  input  in_5,
  input  in_6,
  input  in_7,
  input  in_8,
  output Y,
  output out_10,
  output out_11,
  output out_12
);

  wire and_1_out, and_2_out, and_3_out, and_4_out, and_5_out, and_6_out, not_1_out, not_2_out, not_3_out,
       not_4_out, not_5_out, not_6_out, or_2_out, transistor_1_out, transistor_2_out;

  not not_1 (not_1_out, in_3);
  not not_2 (not_2_out, in_4);
  not not_3 (not_3_out, in_5);
  not not_4 (not_4_out, in_6);
  not not_5 (not_5_out, in_7);
  not not_6 (not_6_out, in_8);
  Transistor #(.\type ("n")) transistor_1 (.in(1'b0), .out(transistor_1_out), .gate(A));
  and and_1 (and_1_out, not_1_out, in_4);
  and and_2 (and_2_out, in_3, not_2_out);
  and and_3 (and_3_out, not_3_out, in_6);
  and and_4 (and_4_out, in_5, not_4_out);
  Transistor transistor_2 (.in(1'b1), .out(transistor_2_out), .gate(A));
  Transistor transistor_3 (.in(transistor_2_out), .out(transistor_1_out), .gate(B));
  Transistor #(.\type ("n")) transistor_4 (.in(1'b0), .out(transistor_1_out), .gate(B));
  and and_5 (and_5_out, not_5_out, not_6_out);
  and and_6 (and_6_out, in_7, in_8);
  or or_1 (out_10, and_1_out, and_2_out);
  or or_2 (or_2_out, and_3_out, and_4_out);
  Transistor transistor_5 (.in(1'b1), .out(Y), .gate(transistor_1_out));
  Transistor #(.\type ("n")) transistor_6 (.in(1'b0), .out(Y), .gate(transistor_1_out));
  not not_7 (out_11, or_2_out);
  or or_3 (out_12, and_5_out, and_6_out);

  // Notes on the sheet:
  //   或门
  //   异或门
  //   同或门1
  //   同或门2
  //   N1
  //   P1
  //   P2
  //   N2
  //   P3
  //   N3
endmodule
