// Logisim project SequentialLogic.circ as structural Verilog: 7 circuits, main circuit main
module main (
  input  RE,
  input  EN,
  input  RE_2,
  input  in_4,
  input  in_5,
  input  D,
  input  RE_3,
  input  RE_4,
  input  in_9,
  input  EN_2,
  input  D_2,
  input  RE_5,
  output out_13,
  output out_14,
  output Q,
  output nQ,
  output Q_2,
  output nQ_2,
  output Q_3,
  output nQ_3,
  output nQ_4,
  output out_22,
  output out_23,
  output out_24,
  output out_25
);

  wire adder_4_1_cout, and_1_out, and_2_out, and_3_out, and_4_out, and_5_out, and_6_out, and_7_out,
       and_8_out, and_9_out, and_10_out, and_11_out, and_12_out, and_13_out, button_1_out, button_2_out,
       button_3_out, button_4_out, button_5_out, button_6_out, button_7_out, d_latch_1_q, d_latch_2_q,
       d_latch_3_q, d_latch_4_q, d_latch_5_q, d_latch_8_q, dipswitch_1_p1, dipswitch_2_p1, dipswitch_3_p1,
       dipswitch_4_p1, dipswitch_5_p1, dipswitch_6_p1, dipswitch_11_p1, dipswitch_12_p1, dipswitch_13_p1,
       dipswitch_14_p1, dipswitch_15_p1, dipswitch_15_p2, dipswitch_15_p3, dipswitch_15_p4, nor_1_out,
       nor_2_out, nor_3_out, not_1_out, not_2_out, not_3_out, not_4_out, not_5_out, not_6_out, not_7_out,
       not_8_out, not_9_out, not_10_out, not_11_out, not_12_out, not_13_out, not_15_out, or_1_out, or_2_out,
       or_3_out, seven_segment_circuit16_1_a, seven_segment_circuit16_1_b, seven_segment_circuit16_1_c,
       seven_segment_circuit16_1_d, seven_segment_circuit16_1_e, seven_segment_circuit16_1_f,
       seven_segment_circuit16_1_g, seven_segment_circuit16_2_a, seven_segment_circuit16_2_b,
       seven_segment_circuit16_2_c, seven_segment_circuit16_2_d, seven_segment_circuit16_2_e,
       seven_segment_circuit16_2_f, seven_segment_circuit16_2_g, sr_latch_3_q, undriven;
  wire [3:0] adder_4_1_s, d_flip_flop_1_q, register_4_1_o;

  // DipSwitch #(.number(1)) dipswitch_1: pin names not known; wires that end beside it: dipswitch_1_p1
  // DipSwitch #(.number(1)) dipswitch_2: pin names not known; wires that end beside it: dipswitch_2_p1
  // DipSwitch #(.number(1)) dipswitch_3: pin names not known; wires that end beside it: dipswitch_3_p1
  // DipSwitch #(.number(1)) dipswitch_4: pin names not known; wires that end beside it: dipswitch_4_p1
  not not_1 (not_1_out, dipswitch_1_p1);
  // DipSwitch #(.number(1)) dipswitch_5: pin names not known; wires that end beside it: dipswitch_5_p1
  // DipSwitch #(.number(1)) dipswitch_6: pin names not known; wires that end beside it: dipswitch_6_p1
  // DipSwitch #(.number(1)) dipswitch_7: pin names not known
  buf and_1 (and_1_out, dipswitch_2_p1);  // AND_Gate
  buf and_2 (and_2_out, dipswitch_2_p1);  // AND_Gate
  // DipSwitch #(.number(1)) dipswitch_8: pin names not known
  // DipSwitch #(.number(1)) dipswitch_9: pin names not known
  buf and_3 (and_3_out, dipswitch_3_p1);  // AND_Gate
  buf and_4 (and_4_out, dipswitch_3_p1);  // AND_Gate
  // DipSwitch #(.number(1)) dipswitch_10: pin names not known
  not not_2 (not_2_out, dipswitch_11_p1);
  // DipSwitch #(.number(1)) dipswitch_11: pin names not known; wires that end beside it: dipswitch_11_p1
  not not_3 (not_3_out, dipswitch_12_p1);
  // DipSwitch #(.number(1)) dipswitch_12: pin names not known; wires that end beside it: dipswitch_12_p1
  not not_4 (not_4_out, button_1_out);
  Button button_1 (.out(button_1_out));
  Button button_2 (.out(button_2_out));
  not not_5 (not_5_out, D);
  Button button_3 (.out(button_3_out));
  not not_6 (not_6_out, not_15_out);
  Button button_4 (.out(button_4_out));
  Button button_5 (.out(button_5_out));
  not not_7 (not_7_out, D_2);
  and and_5 (and_5_out, dipswitch_1_p1, dipswitch_4_p1);
  and and_6 (and_6_out, dipswitch_4_p1, not_1_out);
  and and_7 (and_7_out, dipswitch_5_p1, not_2_out);
  // DipSwitch #(.number(1)) dipswitch_13: pin names not known; wires that end beside it: dipswitch_13_p1
  or or_1 (or_1_out, dipswitch_11_p1, not_8_out);
  not not_8 (not_8_out, dipswitch_5_p1);
  and and_8 (and_8_out, undriven, not_3_out);
  // DipSwitch #(.number(1)) dipswitch_14: pin names not known; wires that end beside it: dipswitch_14_p1
  or or_2 (or_2_out, dipswitch_12_p1, not_9_out);
  not not_9 (not_9_out, undriven);
  not not_10 (not_10_out, button_2_out);
  nor nor_1 (nor_1_out, not_5_out, RE_3);
  not not_11 (not_11_out, button_3_out);
  nor nor_2 (nor_2_out, not_6_out, RE_4);
  not not_12 (not_12_out, button_4_out);
  not not_13 (not_13_out, button_5_out);
  nor nor_3 (nor_3_out, not_7_out, RE_5);
  nor nor_4 (out_13, and_1_out, out_14);
  nor nor_5 (out_14, out_13, and_2_out);
  nand nand_1 (Q, and_3_out, nQ);
  nand nand_2 (nQ, Q, and_4_out);
  and and_9 (and_9_out, and_7_out, dipswitch_13_p1);
  and and_10 (and_10_out, dipswitch_13_p1, or_1_out);
  and and_11 (and_11_out, and_8_out, dipswitch_14_p1);
  and and_12 (and_12_out, dipswitch_14_p1, or_2_out);
  and and_13 (and_13_out, EN_2, button_5_out);
  SR_Latch sr_latch_1 (.R(and_6_out), .S(and_5_out), .Q(Q_2), .NQ(nQ_2));
  D_Latch d_latch_1 (.WE(not_4_out), .D(in_5), .Q(d_latch_1_q));  // open: NQ
  D_Latch d_latch_2 (.WE(not_10_out), .D(nor_1_out), .Q(d_latch_2_q));  // open: NQ
  D_Latch d_latch_3 (.WE(not_11_out), .D(nor_2_out), .Q(d_latch_3_q));  // open: NQ
  D_Latch d_latch_4 (.WE(button_4_out), .D(in_9), .Q(d_latch_4_q));  // open: NQ
  D_Latch d_latch_5 (.WE(not_13_out), .D(nor_3_out), .Q(d_latch_5_q));  // open: NQ
  Button button_6 (.out(button_6_out));
  SR_Latch sr_latch_2 (.R(and_10_out), .S(and_9_out), .Q(Q_3), .NQ(nQ_3));
  not not_14 (dipswitch_6_p1, sr_latch_3_q);
  SR_Latch sr_latch_3 (.R(and_12_out), .S(and_11_out), .Q(sr_latch_3_q), .NQ(nQ_4));
  D_Latch d_latch_6 (.WE(button_1_out), .D(d_latch_1_q), .Q(out_22));  // open: NQ
  D_Latch d_latch_7 (.WE(button_2_out), .D(d_latch_2_q), .Q(out_23));  // open: NQ
  not not_15 (not_15_out, d_latch_8_q);
  D_Latch d_latch_8 (.WE(button_3_out), .D(d_latch_3_q), .Q(d_latch_8_q));  // open: NQ
  D_Latch d_latch_9 (.WE(not_12_out), .D(d_latch_4_q), .Q(out_24));  // open: NQ
  D_Latch d_latch_10 (.WE(and_13_out), .D(d_latch_5_q), .Q(out_25));  // open: NQ
  D_Flip_Flop d_flip_flop_1 (
    .EN(EN), .clk(button_6_out), .D(dipswitch_15_p1), .RE(RE), .Q(d_flip_flop_1_q[0]));  // open: NQ
  // DipSwitch #(.number(4)) dipswitch_15: pin names not known; wires that end beside it: dipswitch_15_p1, dipswitch_15_p2, dipswitch_15_p3, dipswitch_15_p4
  D_Flip_Flop d_flip_flop_2 (
    .EN(EN), .clk(button_6_out), .D(dipswitch_15_p2), .RE(RE), .Q(d_flip_flop_1_q[1]));  // open: NQ
  or or_3 (or_3_out, RE_2, adder_4_1_cout);
  Button button_7 (.out(button_7_out));
  D_Flip_Flop d_flip_flop_3 (
    .EN(EN), .clk(button_6_out), .D(dipswitch_15_p3), .RE(RE), .Q(d_flip_flop_1_q[2]));  // open: NQ
  D_Flip_Flop d_flip_flop_4 (
    .EN(EN), .clk(button_6_out), .D(dipswitch_15_p4), .RE(RE), .Q(d_flip_flop_1_q[3]));  // open: NQ
  seven_segment_circuit16 seven_segment_circuit16_1 (
    .in_1(d_flip_flop_1_q), .a(seven_segment_circuit16_1_a), .b(seven_segment_circuit16_1_b),
    .c(seven_segment_circuit16_1_c), .d(seven_segment_circuit16_1_d), .e(seven_segment_circuit16_1_e),
    .f(seven_segment_circuit16_1_f), .g(seven_segment_circuit16_1_g));
  Register_4 register_4_1 (.D(adder_4_1_s), .RE(or_3_out), .EN(in_4), .clk(button_7_out), .O(register_4_1_o));
  seven_segment_circuit16 seven_segment_circuit16_2 (
    .in_1(adder_4_1_s), .a(seven_segment_circuit16_2_a), .b(seven_segment_circuit16_2_b),
    .c(seven_segment_circuit16_2_c), .d(seven_segment_circuit16_2_d), .e(seven_segment_circuit16_2_e),
    .f(seven_segment_circuit16_2_f), .g(seven_segment_circuit16_2_g));
  _7_Segment_Display u_7_segment_display_1 (
    .g(seven_segment_circuit16_1_g), .f(seven_segment_circuit16_1_f), .a(seven_segment_circuit16_1_a),
    .b(seven_segment_circuit16_1_b), .e(seven_segment_circuit16_1_e), .d(seven_segment_circuit16_1_d),
    .c(seven_segment_circuit16_1_c));  // open: dp
  _7_Segment_Display u_7_segment_display_2 (
    .g(seven_segment_circuit16_2_g), .f(seven_segment_circuit16_2_f), .a(seven_segment_circuit16_2_a),
    .b(seven_segment_circuit16_2_b), .e(seven_segment_circuit16_2_e), .d(seven_segment_circuit16_2_d),
    .c(seven_segment_circuit16_2_c));  // open: dp
  adder_4 adder_4_1 (.A(4'b0001), .B(register_4_1_o), .Cout(adder_4_1_cout), .S(adder_4_1_s));

  // Notes on the sheet:
  //   D锁存器
  //   D
  //   D触发器
  //   SR锁存器
  //   ~S~R锁存器
  //   R
  //   S
  //   WE
  //   带复位的D锁存器
  //   R
  //   D
  //   D锁存器实现位翻转功能
  //   R
  //   D
  //   带复位的D触发器
  //   D触发器实现位翻转
  //   下降沿D触发器
  //   带使能的D触发器
  //   WE
  //   WE
  //   4位寄存器
  //   clk
  //   Q
  //   4位计数器
endmodule

module SR_Latch (
  input  R,
  input  S,
  output Q,
  output NQ
);

  nor nor_1 (Q, R, NQ);
  nor nor_2 (NQ, Q, S);

  // Notes on the sheet:
  //   SR锁存器
endmodule

module D_Latch (
  input  WE,
  input  D,
  output Q,
  output NQ
);

  wire and_1_out, and_2_out, not_1_out;

  not not_1 (not_1_out, D);
  and and_1 (and_1_out, D, WE);
  and and_2 (and_2_out, WE, not_1_out);
  SR_Latch sr_latch_1 (.R(and_2_out), .S(and_1_out), .Q(Q), .NQ(NQ));

  // Notes on the sheet:
  //   D
  //   D锁存器
  //   WE
  //   Q
  //   ~Q
endmodule

module D_Flip_Flop (
  input  EN,
  input  clk,
  input  D,
  input  RE,
  output Q,
  output NQ
);

  wire and_1_out, d_latch_1_q, nor_1_out, not_1_out, not_2_out;

  not not_1 (not_1_out, D);
  and and_1 (and_1_out, EN, clk);
  not not_2 (not_2_out, clk);
  nor nor_1 (nor_1_out, not_1_out, RE);
  D_Latch d_latch_1 (.WE(not_2_out), .D(nor_1_out), .Q(d_latch_1_q));  // open: NQ
  D_Latch d_latch_2 (.WE(and_1_out), .D(d_latch_1_q), .Q(Q), .NQ(NQ));

  // Notes on the sheet:
  //   带使能的D触发器
endmodule

module Register_4 (
  input  [3:0] D,
  input  RE,
  input  EN,
  input  clk,
  output [3:0] O
);

  D_Flip_Flop d_flip_flop_1 (.EN(EN), .clk(clk), .D(D[0]), .RE(RE), .Q(O[0]));  // open: NQ
  D_Flip_Flop d_flip_flop_2 (.EN(EN), .clk(clk), .D(D[1]), .RE(RE), .Q(O[1]));  // open: NQ
  D_Flip_Flop d_flip_flop_3 (.EN(EN), .clk(clk), .D(D[2]), .RE(RE), .Q(O[2]));  // open: NQ
  D_Flip_Flop d_flip_flop_4 (.EN(EN), .clk(clk), .D(D[3]), .RE(RE), .Q(O[3]));  // open: NQ

  // Notes on the sheet:
  //   4位寄存器
endmodule

module Register_8 (
  input  [7:0] D,
  input  RE,
  input  EN,
  input  clk,
  output [7:0] O
);

  D_Flip_Flop d_flip_flop_1 (.EN(EN), .clk(clk), .D(D[0]), .RE(RE), .Q(O[0]));  // open: NQ
  D_Flip_Flop d_flip_flop_2 (.EN(EN), .clk(clk), .D(D[1]), .RE(RE), .Q(O[1]));  // open: NQ
  D_Flip_Flop d_flip_flop_3 (.EN(EN), .clk(clk), .D(D[2]), .RE(RE), .Q(O[2]));  // open: NQ
  D_Flip_Flop d_flip_flop_4 (.EN(EN), .clk(clk), .D(D[3]), .RE(RE), .Q(O[3]));  // open: NQ
  D_Flip_Flop d_flip_flop_5 (.EN(EN), .clk(clk), .D(D[4]), .RE(RE), .Q(O[4]));  // open: NQ
  D_Flip_Flop d_flip_flop_6 (.EN(EN), .clk(clk), .D(D[5]), .RE(RE), .Q(O[5]));  // open: NQ
  D_Flip_Flop d_flip_flop_7 (.EN(EN), .clk(clk), .D(D[6]), .RE(RE), .Q(O[6]));  // open: NQ
  D_Flip_Flop d_flip_flop_8 (.EN(EN), .clk(clk), .D(D[7]), .RE(RE), .Q(O[7]));  // open: NQ

  // Notes on the sheet:
  //   8位寄存器
endmodule

module adder_8 (
  input  [7:0] A,
  input  [7:0] B,
  output Cout,
  output [7:0] S
);

  wire full_adder_1_cout, full_adder_2_cout, full_adder_3_cout, full_adder_4_cout, full_adder_5_cout,
       full_adder_6_cout, half_adder_1_c;

  Half_adder half_adder_1 (.in_1(A[0]), .in_2(B[0]), .S(S[0]), .C(half_adder_1_c));
  Full_Adder full_adder_1 (.Cin(half_adder_1_c), .A(A[1]), .B(B[1]), .Cout(full_adder_1_cout), .S(S[1]));
  Full_Adder full_adder_2 (.Cin(full_adder_1_cout), .A(A[2]), .B(B[2]), .Cout(full_adder_2_cout), .S(S[2]));
  Full_Adder full_adder_3 (.Cin(full_adder_2_cout), .A(A[3]), .B(B[3]), .Cout(full_adder_3_cout), .S(S[3]));
  Full_Adder full_adder_4 (.Cin(full_adder_3_cout), .A(A[4]), .B(B[4]), .Cout(full_adder_4_cout), .S(S[4]));
  Full_Adder full_adder_5 (.Cin(full_adder_4_cout), .A(A[5]), .B(B[5]), .Cout(full_adder_5_cout), .S(S[5]));
  Full_Adder full_adder_6 (.Cin(full_adder_5_cout), .A(A[6]), .B(B[6]), .Cout(full_adder_6_cout), .S(S[6]));
  Full_Adder full_adder_7 (.Cin(full_adder_6_cout), .A(A[7]), .B(B[7]), .Cout(Cout), .S(S[7]));
endmodule
