// Logisim project sCPU.circ as structural Verilog: 1 circuit, main circuit main
module main (
  input  [2:0] in_1,
  output [7:0] out_2
);

  Multiplexer #(.select(3), .width(8)) multiplexer_1 (
    .in0(8'h8a), .in1(8'h90), .in2(8'ha0), .in3(8'hb1), .in4(8'h17), .in5(8'h29), .in6(8'hd1), .in7(8'hdf),
    .out(out_2), .sel(in_1));

  // Notes on the sheet:
  //   多路选择器实现数列求和的指令ROM
endmodule
