// Logisim project minirv.circ as structural Verilog: 11 circuits, main circuit main
module main (
  input  in_1
);

  wire addiop, addop, clk, comparator_1_eq, comparator_2_eq, comparator_3_eq, comparator_4_eq,
       comparator_6_eq, comparator_7_eq, comparator_8_eq, comparator_9_eq, comparator_10_eq,
       comparator_11_eq, comparator_12_eq, jalrop, luiop, lwop, ram_BE0, ram_BE1, ram_BE2, ram_BE3, ram_OE,
       ram_WE, swop, wen;
  wire [2:0] priority_encoder_1_out, priority_encoder_2_out, priority_encoder_3_out, rom_t3_1_out_2_3;
  wire [4:0] add_rd, add_rs1, add_rs2, addi_rd, addi_rs1, and_14_out, and_15_out, and_16_out, and_17_out,
       and_18_out, and_19_out, and_20_out, and_21_out, and_22_out, and_23_out, and_24_out, and_25_out,
       bit_extender_9_out, bit_extender_10_out, bit_extender_11_out, bit_extender_12_out,
       bit_extender_13_out, bit_extender_14_out, bit_extender_15_out, bit_extender_16_out,
       bit_extender_17_out, bit_extender_18_out, bit_extender_19_out, bit_extender_20_out, jalr_rd, jalr_rs1,
       lui_rd, lw_rd, lw_rs1, raddr1, raddr2, sw_rs1, sw_rs2, waddr;
  wire [6:0] rom_t3_1_out_2, rom_t3_1_out_2_4;
  wire [24:7] rom_t3_1_out_2_2;
  wire [31:0] add_rddata, add_rs1data, add_rs2data, adder_1_out, addi_rddata, addi_rs1data, and_1_out,
       and_2_out, and_3_out, and_9_out, and_10_out, and_11_out, and_12_out, and_13_out, bit_extender_1_out,
       bit_extender_2_out, bit_extender_3_out, bit_extender_4_out, bit_extender_5_out, bit_extender_6_out,
       bit_extender_7_out, bit_extender_8_out, jalr_newpc, jalr_rddata, jalr_rs1data, lui_rddata,
       lw_ram_addr, lw_ram_data, lw_rddata, lw_rs1data, multiplexer_1_out, PC, ram_A, ram_RD, ram_WD, rdata1,
       rdata2, sw_ram_addr, sw_ram_data, sw_rs1data, sw_rs2data, undriven, wdata;

  assign bit_extender_1_out = {{31{swop}}, swop};  // Bit_Extender bit_extender_1
  assign and_1_out = bit_extender_1_out & sw_ram_data;  // AND_Gate and_1, 32 bits wide
  buf or_1 (ram_WE, swop);  // OR_Gate
  Clock clock_1 (.out(clk));
  assign ram_WD = and_1_out;  // OR_Gate or_2, 32 bits wide OR_Gate
  Register #(.width(32)) u_PC (.D(multiplexer_1_out), .en(in_1), .clk(clk), .Q(PC));  // open: clr
  RAM #(.addrWidth(16), .asyncread("true"), .byteenables("byteEnables"), .dataWidth(32), .\type ("nonvolatile")) ram_1 (
    .addr(ram_A[15:0]), .we(ram_WE), .oe(ram_OE), .clk(clk), .din(ram_WD), .dout(ram_RD), .be3(ram_BE3),
    .be2(ram_BE2), .be1(ram_BE1), .be0(ram_BE0));
  Adder #(.width(32)) adder_1 (.a(32'h4), .b(PC), .out(adder_1_out));  // open: cin, cout
  Multiplexer #(.width(32)) multiplexer_1 (.in0(adder_1_out), .in1(jalr_newpc), .out(multiplexer_1_out), .sel(jalrop));
  assign bit_extender_2_out = {{31{lwop}}, lwop};  // Bit_Extender bit_extender_2
  assign and_2_out = bit_extender_2_out & lw_ram_addr;  // AND_Gate and_2, 32 bits wide
  assign bit_extender_3_out = {{31{swop}}, swop};  // Bit_Extender bit_extender_3
  assign and_3_out = bit_extender_3_out & sw_ram_addr;  // AND_Gate and_3, 32 bits wide
  buf or_3 (ram_OE, lwop);  // OR_Gate
  ROM_t1 rom_t1_1 ();  // open: in_1, out_2
  ROM_t2 rom_t2_1 (.in_1(undriven));  // open: out_2
  ROM_t3 rom_t3_1 (
    .in_1(PC),
    .out_2({rom_t3_1_out_2_4, rom_t3_1_out_2_2[24:15], rom_t3_1_out_2_3, rom_t3_1_out_2_2[11:7], rom_t3_1_out_2}));
  assign ram_A = and_2_out | and_3_out;  // OR_Gate or_4, 32 bits wide
  Demultiplexer #(.select(3), .width(32)) demultiplexer_1 (
    .out0(lw_rddata), .in(ram_RD), .sel(priority_encoder_1_out));  // open: out1, out2, out3, out4, out5, out6, out7
  Priority_Encoder priority_encoder_1 (
    .in0(lwop), .in1(1'b0), .in2(1'b0), .in3(1'b0), .in4(1'b0), .in5(1'b0), .in6(1'b0), .in7(1'b0),
    .out(priority_encoder_1_out));  // open: en_in, gs, en_out
  Comparator #(.width(3)) comparator_1 (.a(rom_t3_1_out_2_3), .b(3'b010), .eq(comparator_1_eq));  // open: gt, lt
  Comparator #(.width(7)) comparator_2 (.a(rom_t3_1_out_2), .b(7'b0100011), .eq(comparator_2_eq));  // open: gt, lt
  Comparator #(.width(3)) comparator_3 (.a(rom_t3_1_out_2_3), .b(3'b010), .eq(comparator_3_eq));  // open: gt, lt
  Comparator #(.width(7)) comparator_4 (.a(rom_t3_1_out_2), .b(7'b0000011), .eq(comparator_4_eq));  // open: gt, lt
  Comparator #(.width(7)) comparator_5 (.a(rom_t3_1_out_2), .b(7'b0110111), .eq(luiop));  // open: gt, lt
  Comparator #(.width(3)) comparator_6 (.a(rom_t3_1_out_2_3), .b(3'b000), .eq(comparator_6_eq));  // open: gt, lt
  Comparator #(.width(7)) comparator_7 (.a(rom_t3_1_out_2), .b(7'b1100111), .eq(comparator_7_eq));  // open: gt, lt
  Comparator #(.width(7)) comparator_8 (.a(rom_t3_1_out_2), .b(7'b0010011), .eq(comparator_8_eq));  // open: gt, lt
  Comparator #(.width(3)) comparator_9 (.a(3'b000), .b(rom_t3_1_out_2_3), .eq(comparator_9_eq));  // open: gt, lt
  Comparator #(.width(7)) comparator_10 (.a(rom_t3_1_out_2), .b(7'b0110011), .eq(comparator_10_eq));  // open: gt, lt
  Comparator #(.width(7)) comparator_11 (.a({7{1'b0}}), .b(rom_t3_1_out_2_4), .eq(comparator_11_eq));  // open: gt, lt
  Comparator #(.width(3)) comparator_12 (.a(3'b000), .b(rom_t3_1_out_2_3), .eq(comparator_12_eq));  // open: gt, lt
  and and_4 (swop, comparator_1_eq, comparator_2_eq);
  and and_5 (lwop, comparator_3_eq, comparator_4_eq);
  and and_6 (jalrop, comparator_6_eq, comparator_7_eq);
  and and_7 (addiop, comparator_8_eq, comparator_9_eq);
  and and_8 (addop, comparator_10_eq, comparator_11_eq, comparator_12_eq);
  or or_5 (wen, jalrop, luiop, addop, addiop, lwop);
  assign bit_extender_4_out = {{31{jalrop}}, jalrop};  // Bit_Extender bit_extender_4
  assign and_9_out = bit_extender_4_out & jalr_rddata;  // AND_Gate and_9, 32 bits wide
  assign bit_extender_5_out = {{31{addop}}, addop};  // Bit_Extender bit_extender_5
  assign and_10_out = lui_rddata & bit_extender_6_out;  // AND_Gate and_10, 32 bits wide
  assign bit_extender_6_out = {{31{luiop}}, luiop};  // Bit_Extender bit_extender_6
  assign and_11_out = addi_rddata & bit_extender_7_out;  // AND_Gate and_11, 32 bits wide
  assign bit_extender_7_out = {{31{addiop}}, addiop};  // Bit_Extender bit_extender_7
  assign and_12_out = lw_rddata & bit_extender_8_out;  // AND_Gate and_12, 32 bits wide
  assign bit_extender_8_out = {{31{lwop}}, lwop};  // Bit_Extender bit_extender_8
  assign bit_extender_9_out = {{4{jalrop}}, jalrop};  // Bit_Extender bit_extender_9
  assign bit_extender_10_out = {{4{luiop}}, luiop};  // Bit_Extender bit_extender_10
  assign bit_extender_11_out = {{4{addiop}}, addiop};  // Bit_Extender bit_extender_11
  assign bit_extender_12_out = {{4{lwop}}, lwop};  // Bit_Extender bit_extender_12
  assign and_13_out = add_rddata & bit_extender_5_out;  // AND_Gate and_13, 32 bits wide
  assign and_14_out = bit_extender_9_out & jalr_rd;  // AND_Gate and_14, 5 bits wide
  assign and_15_out = add_rd & bit_extender_13_out;  // AND_Gate and_15, 5 bits wide
  assign bit_extender_13_out = {{4{addop}}, addop};  // Bit_Extender bit_extender_13
  assign and_16_out = lui_rd & bit_extender_10_out;  // AND_Gate and_16, 5 bits wide
  assign and_17_out = addi_rd & bit_extender_11_out;  // AND_Gate and_17, 5 bits wide
  assign and_18_out = lw_rd & bit_extender_12_out;  // AND_Gate and_18, 5 bits wide
  assign wdata = and_9_out | and_13_out | and_10_out | and_11_out | and_12_out;  // OR_Gate or_6, 32 bits wide
  assign waddr = and_14_out | and_15_out | and_16_out | and_17_out | and_18_out;  // OR_Gate or_7, 5 bits wide
  my_sw my_sw_1 (
    .I({rom_t3_1_out_2_4, rom_t3_1_out_2_2[24:15], rom_t3_1_out_2_3, rom_t3_1_out_2_2[11:7], rom_t3_1_out_2}),
    .rs1data(sw_rs1data), .rs2data(sw_rs2data), .rs1(sw_rs1), .rs2(sw_rs2), .ram_addr(sw_ram_addr),
    .ram_data(sw_ram_data));
  my_lw my_lw_1 (
    .I({rom_t3_1_out_2_4, rom_t3_1_out_2_2[24:15], rom_t3_1_out_2_3, rom_t3_1_out_2_2[11:7], rom_t3_1_out_2}),
    .rs1data(lw_rs1data), .ram_data(lw_ram_data), .rd(lw_rd), .rs1(lw_rs1), .ram_addr(lw_ram_addr),
    .rddata(lw_rddata));
  my_lui my_lui_1 (
    .I({rom_t3_1_out_2_4, rom_t3_1_out_2_2[24:15], rom_t3_1_out_2_3, rom_t3_1_out_2_2[11:7], rom_t3_1_out_2}),
    .rd(lui_rd), .rddata(lui_rddata));
  my_add my_add_1 (
    .I({rom_t3_1_out_2_4, rom_t3_1_out_2_2[24:15], rom_t3_1_out_2_3, rom_t3_1_out_2_2[11:7], rom_t3_1_out_2}),
    .rs2data(add_rs2data), .rs1data(add_rs1data), .rd(add_rd), .rs1(add_rs1), .rs2(add_rs2),
    .rddata(add_rddata));
  my_jalr my_jalr_1 (
    .I({rom_t3_1_out_2_4, rom_t3_1_out_2_2[24:15], rom_t3_1_out_2_3, rom_t3_1_out_2_2[11:7], rom_t3_1_out_2}),
    .rs1data(jalr_rs1data), .PC(PC), .rd(jalr_rd), .rs1(jalr_rs1), .newpc(jalr_newpc), .rddata(jalr_rddata));
  my_addi my_addi_1 (
    .I({rom_t3_1_out_2_4, rom_t3_1_out_2_2[24:15], rom_t3_1_out_2_3, rom_t3_1_out_2_2[11:7], rom_t3_1_out_2}),
    .rs1data(addi_rs1data), .rd(addi_rd), .rs1(addi_rs1), .rddata(addi_rddata));
  assign bit_extender_14_out = {{4{swop}}, swop};  // Bit_Extender bit_extender_14
  assign bit_extender_15_out = {{4{jalrop}}, jalrop};  // Bit_Extender bit_extender_15
  assign bit_extender_16_out = {{4{addop}}, addop};  // Bit_Extender bit_extender_16
  assign bit_extender_17_out = {{4{lwop}}, lwop};  // Bit_Extender bit_extender_17
  assign bit_extender_18_out = {{4{addiop}}, addiop};  // Bit_Extender bit_extender_18
  assign and_19_out = sw_rs1 & bit_extender_14_out;  // AND_Gate and_19, 5 bits wide
  assign and_20_out = bit_extender_15_out & jalr_rs1;  // AND_Gate and_20, 5 bits wide
  assign and_21_out = add_rs1 & bit_extender_16_out;  // AND_Gate and_21, 5 bits wide
  assign and_22_out = lw_rs1 & bit_extender_17_out;  // AND_Gate and_22, 5 bits wide
  assign and_23_out = addi_rs1 & bit_extender_18_out;  // AND_Gate and_23, 5 bits wide
  Demultiplexer #(.select(3), .width(32)) demultiplexer_2 (
    .out0(addi_rs1data), .out1(jalr_rs1data), .out2(add_rs1data), .out3(lw_rs1data), .out4(sw_rs1data),
    .in(rdata1), .sel(priority_encoder_2_out));  // open: out5, out6, out7
  Priority_Encoder priority_encoder_2 (
    .in0(addiop), .in1(jalrop), .in2(addop), .in3(lwop), .in4(swop), .in5(1'b0), .in6(1'b0), .in7(1'b0),
    .out(priority_encoder_2_out));  // open: en_in, gs, en_out
  assign raddr1 = and_19_out | and_20_out | and_21_out | and_22_out | and_23_out;  // OR_Gate or_8, 5 bits wide
  GPR gpr_1 (
    .clk(clk), .wdata(wdata), .waddr(waddr), .wen(wen), .raddr1(raddr1), .raddr2(raddr2), .rdata1(rdata1),
    .rdata2(rdata2));
  assign and_24_out = add_rs2 & bit_extender_19_out;  // AND_Gate and_24, 5 bits wide
  assign bit_extender_19_out = {{4{addop}}, addop};  // Bit_Extender bit_extender_19
  assign and_25_out = sw_rs2 & bit_extender_20_out;  // AND_Gate and_25, 5 bits wide
  assign bit_extender_20_out = {{4{swop}}, swop};  // Bit_Extender bit_extender_20
  Demultiplexer #(.select(3), .width(32)) demultiplexer_3 (
    .out0(add_rs2data), .out1(sw_rs2data), .in(rdata2), .sel(priority_encoder_3_out));  // open: out2, out3, out4, out5, out6, out7
  Priority_Encoder priority_encoder_3 (
    .in0(addop), .in1(swop), .in2(1'b0), .in3(1'b0), .in4(1'b0), .in5(1'b0), .in6(1'b0), .in7(1'b0),
    .out(priority_encoder_3_out));  // open: en_in, gs, en_out
  assign raddr2 = and_24_out | and_25_out;  // OR_Gate or_9, 5 bits wide

  // Notes on the sheet:
  //   RAM写
  //   RAM读
  //   opcode
  //   funct3
  //   funct7
  //   lw
  //   lw
  //   lui
  //   jalr
  //   addi
  //   RAM读
  //   addi
  //   写端口
  //   读1
  //   读2
endmodule

module GPR (
  input  clk,
  input  [31:0] wdata,
  input  [4:0] waddr,
  input  wen,
  input  [4:0] raddr1,
  input  [4:0] raddr2,
  output [31:0] rdata1,
  output [31:0] rdata2
);

  wire decoder_1_out1, decoder_1_out2, decoder_1_out3, decoder_1_out4, decoder_1_out5, decoder_1_out6,
       decoder_1_out7, decoder_1_out8, decoder_1_out9, decoder_1_out10, decoder_1_out11, decoder_1_out12,
       decoder_1_out13, decoder_1_out14, decoder_1_out15;
  wire [31:0] register_1_q, register_2_q, register_3_q, register_4_q, register_5_q, register_6_q,
       register_7_q, register_8_q, register_9_q, register_10_q, register_11_q, register_12_q, register_13_q,
       register_14_q, register_15_q, register_16_q;

  Decoder #(.select(4)) decoder_1 (
    .out1(decoder_1_out1), .out2(decoder_1_out2), .out3(decoder_1_out3), .out4(decoder_1_out4),
    .out5(decoder_1_out5), .out6(decoder_1_out6), .out7(decoder_1_out7), .out8(decoder_1_out8),
    .out9(decoder_1_out9), .out10(decoder_1_out10), .out11(decoder_1_out11), .out12(decoder_1_out12),
    .out13(decoder_1_out13), .out14(decoder_1_out14), .out15(decoder_1_out15), .sel(waddr[3:0]), .en(wen));  // open: out0
  Register #(.width(32)) register_1 (.D(wdata), .en(decoder_1_out1), .clk(clk), .Q(register_1_q), .clr(1'b1));
  Register #(.width(32)) register_2 (.D(wdata), .en(decoder_1_out8), .clk(clk), .Q(register_2_q));  // open: clr
  Register #(.width(32)) register_3 (.D(wdata), .en(decoder_1_out1), .clk(clk), .Q(register_3_q));  // open: clr
  Register #(.width(32)) register_4 (.D(wdata), .en(decoder_1_out9), .clk(clk), .Q(register_4_q));  // open: clr
  Register #(.width(32)) register_5 (.D(wdata), .en(decoder_1_out2), .clk(clk), .Q(register_5_q));  // open: clr
  Register #(.width(32)) register_6 (.D(wdata), .en(decoder_1_out10), .clk(clk), .Q(register_6_q));  // open: clr
  Register #(.width(32)) register_7 (.D(wdata), .en(decoder_1_out3), .clk(clk), .Q(register_7_q));  // open: clr
  Register #(.width(32)) register_8 (.D(wdata), .en(decoder_1_out11), .clk(clk), .Q(register_8_q));  // open: clr
  Register #(.width(32)) register_9 (.D(wdata), .en(decoder_1_out4), .clk(clk), .Q(register_9_q));  // open: clr
  Register #(.width(32)) register_10 (.D(wdata), .en(decoder_1_out12), .clk(clk), .Q(register_10_q));  // open: clr
  Register #(.width(32)) register_11 (.D(wdata), .en(decoder_1_out5), .clk(clk), .Q(register_11_q));  // open: clr
  Register #(.width(32)) register_12 (.D(wdata), .en(decoder_1_out13), .clk(clk), .Q(register_12_q));  // open: clr
  Register #(.width(32)) register_13 (.D(wdata), .en(decoder_1_out6), .clk(clk), .Q(register_13_q));  // open: clr
  Register #(.width(32)) register_14 (.D(wdata), .en(decoder_1_out14), .clk(clk), .Q(register_14_q));  // open: clr
  Register #(.width(32)) register_15 (.D(wdata), .en(decoder_1_out7), .clk(clk), .Q(register_15_q));  // open: clr
  Register #(.width(32)) register_16 (.D(wdata), .en(decoder_1_out15), .clk(clk), .Q(register_16_q));  // open: clr
  Multiplexer #(.select(4), .width(32)) multiplexer_1 (
    .in0(register_1_q), .in1(register_3_q), .in2(register_5_q), .in3(register_7_q), .in4(register_9_q),
    .in5(register_11_q), .in6(register_13_q), .in7(register_15_q), .in8(register_2_q), .in9(register_4_q),
    .in10(register_6_q), .in11(register_8_q), .in12(register_10_q), .in13(register_12_q),
    .in14(register_14_q), .in15(register_16_q), .out(rdata1), .sel(raddr1[3:0]));
  Multiplexer #(.select(4), .width(32)) multiplexer_2 (
    .in0(register_1_q), .in1(register_3_q), .in2(register_5_q), .in3(register_7_q), .in4(register_9_q),
    .in5(register_11_q), .in6(register_13_q), .in7(register_15_q), .in8(register_2_q), .in9(register_4_q),
    .in10(register_6_q), .in11(register_8_q), .in12(register_10_q), .in13(register_12_q),
    .in14(register_14_q), .in15(register_16_q), .out(rdata2), .sel(raddr2[3:0]));
endmodule

module ROM_t1 (
  input  [31:0] in_1,
  output [31:0] out_2
);

  ROM #(.dataWidth(32)) rom_1 (.addr(in_1[9:2]), .data(out_2));

  // Notes on the sheet:
  //   contents of rom_1 (hex, n*v repeats v):
  //   ffe00513 10000e7 c000e7 c00067 a50513 8067
endmodule

module my_addi (
  input  [31:0] I,
  input  [31:0] rs1data,
  output [4:0] rd,
  output [4:0] rs1,
  output [31:0] rddata
);

  wire [31:0] bit_extender_1_out;

  assign bit_extender_1_out = {{20{I[31]}}, I[31:20]};  // Bit_Extender bit_extender_1
  Adder #(.width(32)) adder_1 (.a(bit_extender_1_out), .b(rs1data), .out(rddata));  // open: cin, cout

  assign rd = I[11:7];
  assign rs1 = I[19:15];
endmodule

module my_jalr (
  input  [31:0] I,
  input  [31:0] rs1data,
  input  [31:0] PC,
  output [4:0] rd,
  output [4:0] rs1,
  output [31:0] newpc,
  output [31:0] rddata
);

  wire [31:0] bit_extender_1_out;

  assign bit_extender_1_out = {{20{I[31]}}, I[31:20]};  // Bit_Extender bit_extender_1
  Adder #(.width(32)) adder_1 (.a(PC), .b(32'h4), .out(rddata));  // open: cin, cout
  Adder #(.width(32)) adder_2 (.a(bit_extender_1_out), .b(rs1data), .out(newpc));  // open: cin, cout

  assign rd = I[11:7];
  assign rs1 = I[19:15];

  // Notes on the sheet:
  //   把当前的下一条指令地址存入rd
endmodule

module my_add (
  input  [31:0] I,
  input  [31:0] rs2data,
  input  [31:0] rs1data,
  output [4:0] rd,
  output [4:0] rs1,
  output [4:0] rs2,
  output [31:0] rddata
);

  Adder #(.width(32)) adder_1 (.a(rs2data), .b(rs1data), .out(rddata));  // open: cin, cout

  assign rd = I[11:7];
  assign rs1 = I[19:15];
  assign rs2 = I[24:20];
endmodule

module my_lui (
  input  [31:0] I,
  output [4:0] rd,
  output [31:0] rddata
);


  assign rd = I[11:7];
  assign rddata = {I[31:12], {12{1'b0}}};
endmodule

module ROM_t2 (
  input  [31:0] in_1,
  output [31:0] out_2
);

  ROM #(.dataWidth(32)) rom_1 (.addr(in_1[9:2]), .data(out_2));

  // Notes on the sheet:
  //   contents of rom_1 (hex, n*v repeats v):
  //   123450b7 67808093 1000113 2081b3 10067
endmodule

module my_lw (
  input  [31:0] I,
  input  [31:0] rs1data,
  input  [31:0] ram_data,
  output [4:0] rd,
  output [4:0] rs1,
  output [31:0] ram_addr,
  output [31:0] rddata
);

  wire [1:0] adder_1_out;
  wire [31:0] bit_extender_1_out;

  assign bit_extender_1_out = {{20{I[31]}}, I[31:20]};  // Bit_Extender bit_extender_1
  Adder #(.width(32)) adder_1 (
    .a(bit_extender_1_out), .b(rs1data), .out({ram_addr[29:0], adder_1_out}));  // open: cin, cout

  assign ram_addr[31:30] = 2'b00;
  assign rd = I[11:7];
  assign rddata = ram_data;
  assign rs1 = I[19:15];
endmodule

module my_sw (
  input  [31:0] I,
  input  [31:0] rs1data,
  input  [31:0] rs2data,
  output [4:0] rs1,
  output [4:0] rs2,
  output [31:0] ram_addr,
  output [31:0] ram_data
);

  wire [1:0] adder_1_out;
  wire [31:0] bit_extender_1_out;

  assign bit_extender_1_out = {{20{I[31]}}, {I[31:25], I[11:7]}};  // Bit_Extender bit_extender_1
  Adder #(.width(32)) adder_1 (
    .a(bit_extender_1_out), .b(rs1data), .out({ram_addr[29:0], adder_1_out}));  // open: cin, cout

  assign ram_addr[31:30] = 2'b00;
  assign ram_data = rs2data;
  assign rs1 = I[19:15];
  assign rs2 = I[24:20];
endmodule

module ROM_t3 (
  input  [31:0] in_1,
  output [31:0] out_2
);

  ROM #(.dataWidth(32)) rom_1 (.addr(in_1[9:2]), .data(out_2));

  // Notes on the sheet:
  //   contents of rom_1 (hex, n*v repeats v):
  //   40a103 20a023
endmodule
